// Logisim project c17.circ as structural Verilog: 2 circuits, main circuit main
module main (
);

  c17 c17_1 ();  // open: _1_A, _2_B, _3_C, _6_D, _7_E, _22, _23
endmodule

module c17 (
  input  _1_A,
  input  _2_B,
  input  _3_C,
  input  _6_D,
  input  _7_E,
  output _22,
  output _23
);

  wire _1__3_out, _2__11_out, _3__6_out, _11__7_out;

  nand _1__3 (_1__3_out, _1_A, _3_C);
  nand _3__6 (_3__6_out, _3_C, _6_D);
  nand _2__11 (_2__11_out, _2_B, _3__6_out);
  nand _11__7 (_11__7_out, _3__6_out, _7_E);
  nand _10__16 (_22, _1__3_out, _2__11_out);
  nand _16__19 (_23, _2__11_out, _11__7_out);

  // Notes on the sheet:
  //   10
  //   11
  //   16
  //   19
endmodule
